// Digital circuit Control Unit.dig as structural Verilog
module Control_Unit (
  input  [15:0] IR,
  input  CLK,
  input  S,
  input  R,
  input  I,
  input  IEN,
  input  FGI,
  input  FGO,
  input  E,
  input  [15:0] AC,
  input  [15:0] DR,
  input  C_OUT,
  output [6:0] x,
  output S_CLR,
  output I_LD,
  output I_D,
  output R_J,
  output R_K,
  output IEN_J,
  output IEN_K,
  output FGI_K,
  output FGO_K,
  output AR_LD,
  output AR_INR,
  output AR_CLR,
  output MEM_read,
  output MEM_write,
  output PC_LD,
  output PC_INCR,
  output PC_CLR,
  output DR_LD,
  output DR_INCR,
  output AC_LD,
  output AC_INCR,
  output AC_CLR,
  output [6:0] AL_OP,
  output OUTR_LD,
  output IR_LD,
  output TR_LD,
  output [15:0] T,
  output [7:0] D,
  output E_J,
  output E_K
);

  wire and_1_out, and_2_out, and_3_out, and_4_out, E_J_t, E_K_t, not_1_out, not_2_out, not_3_out, or_1_out,
       or_2_out, R_J_t, SC_CLR, SC_ovf;
  wire [3:0] SC;

  ROM #(.AddrBits(9), .Bits(9)) ROM_2 (
    .A({I, R, IR[14:12], SC}), .sel(1'b1), .D({SC_CLR, S_CLR, I_LD, R_J_t, R_K, IEN_J, IEN_K, FGI_K, FGO_K}));
  ROM #(.AddrBits(9), .Bits(16)) ROM_1 (
    .A({I, R, IR[14:12], SC}), .sel(1'b1),
    .D({AR_LD, AR_INR, AR_CLR, MEM_read, MEM_write, PC_LD, PC_INCR, PC_CLR, DR_LD, DR_INCR, AC_LD, AC_INCR, AC_CLR, AL_OP[6:4]}));
  ROM #(.AddrBits(9), .Bits(16)) ROM_0 (
    .A({I, R, IR[14:12], SC}), .sel(1'b1),
    .D({AL_OP[3:0], OUTR_LD, IR_LD, TR_LD, E_J_t, E_K_t, x[0], x[1], x[2], x[3], x[4], x[5], x[6]}));
  or or_1 (or_1_out, S, SC_CLR);
  or or_2 (or_2_out, FGI, FGO);
  not not_1 (not_1_out, T[2]);
  not not_2 (not_2_out, T[1]);
  not not_3 (not_3_out, T[0]);
  D_FF u_I (.D(IR[15]), .C(CLK), .Q(I_D));  // open: nQ
  Counter #(.Bits(4), .isProgramCounter("true")) u_SC (.en(1'b1), .C(CLK), .clr(or_1_out), .out(SC), .ovf(SC_ovf));
  and and_1 (and_1_out, IEN, or_2_out);
  and and_2 (and_2_out, not_1_out, not_2_out, not_3_out);
  and and_3 (and_3_out, and_1_out, and_2_out);
  Decoder #(.Selector_Bits(3)) decoder_1 (
    .sel(IR[14:12]), .out_0(D[0]), .out_1(D[1]), .out_2(D[2]), .out_3(D[3]), .out_4(D[4]), .out_5(D[5]),
    .out_6(D[6]), .out_7(D[7]));
  Decoder #(.Selector_Bits(4)) decoder_2 (
    .sel(SC), .out_0(T[0]), .out_1(T[1]), .out_2(T[2]), .out_3(T[3]), .out_4(T[4]), .out_5(T[5]),
    .out_6(T[6]), .out_7(T[7]), .out_8(T[8]), .out_9(T[9]), .out_10(T[10]), .out_11(T[11]), .out_12(T[12]),
    .out_13(T[13]), .out_14(T[14]), .out_15(T[15]));
  LED led_1 (.in(SC_ovf));
  or or_3 (R_J, R_J_t, and_3_out);
  and and_4 (and_4_out, E_K_t, E_J_t, IR[11]);
  and and_5 (E_J, E, and_4_out);

  assign E_K = E_J;

  // Other names for the same wires on the sheet: D_0 = D[0]; D_1 = D[1]; D_2 = D[2]; D_3 = D[3]; D_4 = D[4];
  //   D_5 = D[5]; D_6 = D[6]; D_7 = D[7]; B_0 = IR[0]; B_1 = IR[1]; B_2 = IR[2]; B_3 = IR[3]; B_4 = IR[4];
  //   B_5 = IR[5]; B_6 = IR[6]; B_7 = IR[7]; B_8 = IR[8]; B_9 = IR[9]; B_10 = IR[10]; B_11 = IR[11];
  //   D_t[2:0] = IR[14:12]; T_0 = T[0]; T_1 = T[1]; T_2 = T[2]; T_3 = T[3]; T_4 = T[4]; T_5 = T[5]; T_6 = T[6];
  //   T_7 = T[7]; T_8 = T[8]; T_9 = T[9]; T_10 = T[10]; T_11 = T[11]; T_12 = T[12]; T_13 = T[13]; T_14 = T[14];
  //   T_15 = T[15]

  // Notes on the sheet:
  //   CLK: Hz: 5
  //   contents of ROM_2 (hex, n*v repeats v):
  //   80,0,40,0,0,100,10*0,80,0,40,13*0,80,0,40,0,0,100,10*0,80,0,40
  //   ,13*0,80,0,40,13*0,80,0,40,13*0,80,0,40,13*0,80,0,40,141*0,80
  //   ,0,40,0,0,100,10*0,80,0,40,13*0,80,0,40,0,0,100,10*0,80,0,40,13*0
  //   ,80,0,40,13*0,80,0,40,13*0,80,0,40,13*0,80,0,40
  //   contents of ROM_1 (hex, n*v repeats v):
  //   8000,1200,8000,0,1080,20,10*0,8000,1200,8000,13*0,8000,1200,8000
  //   ,0,1080,20,10*0,8000,1200,8000,13*0,8000,1200,8000,13*0,8000,1200
  //   ,8000,13*0,8000,1200,8000,13*0,8000,1200,8000,141*0,8000,1200
  //   ,8000,9000,1080,20,10*0,8000,1200,8000,9000,12*0,8000,1200,8000
  //   ,9000,1080,20,10*0,8000,1200,8000,9000,12*0,8000,1200,8000,9000
  //   ,12*0,8000,1200,8000,9000,12*0,8000,1200,8000,9000,12*0,8000,1200,8000
  //   contents of ROM_0 (hex, n*v repeats v):
  //   20,401,4,0,1,1000,10*0,20,401,4,13*0,20,401,4,0,0,4000,10*0,20
  //   ,401,4,13*0,20,401,4,13*0,20,401,4,13*0,20,401,4,13*0,20,401,4
  //   ,180,140*0,20,401,4,1,1,1000,10*0,20,401,4,1,12*0,20,401,4,1,0
  //   ,4000,10*0,20,401,4,1,12*0,20,401,4,1,12*0,20,401,4,1,12*0,20
  //   ,401,4,1,12*0,20,401,4
endmodule
